// Logisim project circ.circ as structural Verilog: 12 circuits, main circuit counter10
module main (
);

  wire Button_1_out, Button_2_out, clock_1_out, d_ff_1_q, DipSwitch_1_sw1, input_ctrl_1_long,
       input_ctrl_1_short, input_ctrl_2_long, input_ctrl_2_short, not_1_out;
  wire [2:0] main_statemachine_1_state_binary;
  wire [6:0] multiplexer_1_out, multiplexer_2_out, multiplexer_3_out, multiplexer_4_out, multiplexer_5_out,
       multiplexer_6_out, State_0_main_clock_x7_2, State_0_main_clock_x7_3, State_0_main_clock_x7_4,
       State_0_main_clock_x7_5, State_0_main_clock_x7_6, State_0_main_clock_x7_7;

  Clock clock_1 (.out(clock_1_out));
  Button Button_1 (.out(Button_1_out));
  Button Button_2 (.out(Button_2_out));
  DipSwitch #(.number(10)) DipSwitch_1 (.sw1(DipSwitch_1_sw1));  // open: sw2, sw3, sw4, sw5, sw6, sw7, sw8, sw9, sw10
  input_ctrl input_ctrl_1 (
    .button(Button_1_out), .clk(clock_1_out), .short(input_ctrl_1_short), .long(input_ctrl_1_long));
  input_ctrl input_ctrl_2 (
    .button(Button_2_out), .clk(clock_1_out), .short(input_ctrl_2_short), .long(input_ctrl_2_long));
  main_statemachine main_statemachine_1 (
    .button1_short(input_ctrl_1_short), .button2_short(input_ctrl_2_short), .dippswitch1(DipSwitch_1_sw1),
    .clk(clock_1_out), .state_binary(main_statemachine_1_state_binary));
  not not_1 (not_1_out, d_ff_1_q);
  D_Flip_Flop d_ff_1 (.D(not_1_out), .clk(input_ctrl_1_long), .Q(d_ff_1_q));  // open: Qn, preset, reset
  clock24h_display State_0_main_clock (
    .clk_10ths(clock_1_out), .set_on(d_ff_1_q), .b1_short(input_ctrl_1_short), .b2_short(input_ctrl_2_short),
    .reset(input_ctrl_2_long), .x7_2(State_0_main_clock_x7_2), .x7_3(State_0_main_clock_x7_3),
    .x7_4(State_0_main_clock_x7_4), .x7_5(State_0_main_clock_x7_5), .x7_6(State_0_main_clock_x7_6),
    .x7_7(State_0_main_clock_x7_7));  // open: x7_0, x7_1
  Multiplexer #(.select(3), .width(7), .enable("false")) multiplexer_1 (
    .in0(State_0_main_clock_x7_7), .in1(7'b0000001), .in2(7'b0000010), .in3(7'b0000100), .in4(7'b0001000),
    .in5(7'b0010000), .in6(7'b0100000), .in7(7'b1000000), .out(multiplexer_1_out),
    .sel(main_statemachine_1_state_binary));
  _7_Segment_Display L_7_Segment_Display_1 (
    .g(multiplexer_1_out[6]), .f(multiplexer_1_out[5]), .a(multiplexer_1_out[0]), .b(multiplexer_1_out[1]),
    .e(multiplexer_1_out[4]), .d(multiplexer_1_out[3]), .c(multiplexer_1_out[2]));  // open: dp
  Multiplexer #(.select(3), .width(7), .enable("false")) multiplexer_2 (
    .in0(State_0_main_clock_x7_6), .out(multiplexer_2_out), .sel(main_statemachine_1_state_binary));  // open: in1, in2, in3, in4, in5, in6, in7
  _7_Segment_Display L_7_Segment_Display_2 (
    .g(multiplexer_2_out[6]), .f(multiplexer_2_out[5]), .a(multiplexer_2_out[0]), .b(multiplexer_2_out[1]),
    .e(multiplexer_2_out[4]), .d(multiplexer_2_out[3]), .c(multiplexer_2_out[2]));  // open: dp
  Multiplexer #(.select(3), .width(7), .enable("false")) multiplexer_3 (
    .in0(State_0_main_clock_x7_5), .out(multiplexer_3_out), .sel(main_statemachine_1_state_binary));  // open: in1, in2, in3, in4, in5, in6, in7
  _7_Segment_Display L_7_Segment_Display_3 (
    .g(multiplexer_3_out[6]), .f(multiplexer_3_out[5]), .a(multiplexer_3_out[0]), .b(multiplexer_3_out[1]),
    .e(multiplexer_3_out[4]), .d(multiplexer_3_out[3]), .c(multiplexer_3_out[2]));  // open: dp
  Multiplexer #(.select(3), .width(7), .enable("false")) multiplexer_4 (
    .in0(State_0_main_clock_x7_4), .out(multiplexer_4_out), .sel(main_statemachine_1_state_binary));  // open: in1, in2, in3, in4, in5, in6, in7
  _7_Segment_Display L_7_Segment_Display_4 (
    .g(multiplexer_4_out[6]), .f(multiplexer_4_out[5]), .a(multiplexer_4_out[0]), .b(multiplexer_4_out[1]),
    .e(multiplexer_4_out[4]), .d(multiplexer_4_out[3]), .c(multiplexer_4_out[2]));  // open: dp
  Multiplexer #(.select(3), .width(7), .enable("false")) multiplexer_5 (
    .in0(State_0_main_clock_x7_3), .out(multiplexer_5_out), .sel(main_statemachine_1_state_binary));  // open: in1, in2, in3, in4, in5, in6, in7
  _7_Segment_Display L_7_Segment_Display_5 (
    .g(multiplexer_5_out[6]), .f(multiplexer_5_out[5]), .a(multiplexer_5_out[0]), .b(multiplexer_5_out[1]),
    .e(multiplexer_5_out[4]), .d(multiplexer_5_out[3]), .c(multiplexer_5_out[2]));  // open: dp
  Multiplexer #(.select(3), .width(7), .enable("false")) multiplexer_6 (
    .in0(State_0_main_clock_x7_2), .out(multiplexer_6_out), .sel(main_statemachine_1_state_binary));  // open: in1, in2, in3, in4, in5, in6, in7
  _7_Segment_Display L_7_Segment_Display_6 (
    .g(multiplexer_6_out[6]), .f(multiplexer_6_out[5]), .a(multiplexer_6_out[0]), .b(multiplexer_6_out[1]),
    .e(multiplexer_6_out[4]), .d(multiplexer_6_out[3]), .c(multiplexer_6_out[2]));  // open: dp

  // Notes on the sheet:
  //   actual state
  //   State 7
  //   state 6
  //   state 5
  //   state 4
  //   state 3
  //   state 2
  //   state 1
endmodule

module counter10 (
  input  b3,
  input  b2,
  input  b1,
  input  b0,
  output b3_out,
  output b2_out,
  output b1_out,
  output b0_out,
  output carry
);

  wire and_1_out, and_2_out, and_3_out, and_4_out, and_5_out, and_6_out, and_7_out, and_8_out, and_9_out,
       not_1_out, not_2_out, not_3_out, not_4_out, not_5_out, not_6_out, not_7_out, not_8_out, not_9_out,
       not_10_out, not_11_out, not_12_out, not_13_out, not_14_out, not_15_out, not_16_out, not_17_out,
       not_18_out, not_19_out, not_20_out, not_21_out, not_22_out, not_23_out;

  not not_1 (not_1_out, b3);
  not not_2 (not_2_out, b2);
  not not_3 (not_3_out, b1);
  not not_4 (not_4_out, b0);
  not not_5 (not_5_out, b3);
  not not_6 (not_6_out, b2);
  not not_7 (not_7_out, b3);
  not not_8 (not_8_out, b1);
  not not_9 (not_9_out, b3);
  not not_10 (not_10_out, b0);
  not not_11 (not_11_out, b3);
  not not_12 (not_12_out, b1);
  not not_13 (not_13_out, b3);
  not not_14 (not_14_out, b0);
  not not_15 (not_15_out, b3);
  not not_16 (not_16_out, b0);
  not not_17 (not_17_out, b2);
  not not_18 (not_18_out, b1);
  not not_19 (not_19_out, b0);
  not not_20 (not_20_out, b3);
  not not_21 (not_21_out, b2);
  not not_22 (not_22_out, b1);
  not not_23 (not_23_out, b0);
  and and_1 (and_1_out, not_1_out, b2, b1, b0);
  and and_2 (and_2_out, b3, not_2_out, not_3_out, not_4_out);
  and and_3 (and_3_out, not_5_out, not_6_out, b1, b0);
  and and_4 (and_4_out, not_7_out, b2, not_8_out);
  and and_5 (and_5_out, not_9_out, b2, not_10_out);
  and and_6 (and_6_out, not_11_out, not_12_out, b0);
  and and_7 (and_7_out, not_13_out, b1, not_14_out);
  and and_8 (and_8_out, not_15_out, not_16_out);
  and and_9 (and_9_out, not_17_out, not_18_out, not_19_out);
  and and_10 (carry, not_20_out, not_21_out, not_22_out, not_23_out);
  or or_1 (b3_out, and_1_out, and_2_out);
  or or_2 (b2_out, and_3_out, and_4_out, and_5_out);
  or or_3 (b1_out, and_6_out, and_7_out);
  or or_4 (b0_out, and_8_out, and_9_out);
endmodule

module bin2display (
  input  b0,
  input  b1,
  input  b2,
  input  b3,
  output a,
  output b,
  output c,
  output d,
  output e,
  output f,
  output g
);

  wire and_1_out, and_2_out, and_3_out, and_4_out, and_5_out, and_6_out, and_7_out, and_8_out, and_9_out,
       and_10_out, and_11_out, and_12_out, and_13_out, and_14_out, and_15_out, and_16_out, and_17_out,
       and_18_out, and_19_out, and_20_out, and_21_out, and_22_out, and_23_out, and_24_out, and_25_out,
       and_26_out, and_27_out, and_28_out, and_29_out, and_30_out, and_31_out, and_32_out, and_33_out,
       and_34_out, and_35_out, not_1_out, not_2_out, not_3_out, not_4_out, not_5_out, not_6_out, not_7_out,
       not_8_out, not_9_out, not_10_out, not_11_out, not_12_out, not_13_out, not_14_out, not_15_out,
       not_16_out, not_17_out, not_18_out, not_19_out, not_20_out, not_21_out, not_22_out, not_23_out,
       not_24_out, not_25_out, not_26_out, not_27_out, not_28_out, not_29_out, not_30_out, not_31_out,
       not_32_out, not_33_out, not_34_out, not_35_out, not_36_out, not_37_out, not_38_out, not_39_out,
       not_40_out, not_41_out, not_42_out, not_43_out;

  not not_1 (not_1_out, b2);
  not not_2 (not_2_out, b0);
  not not_3 (not_3_out, b3);
  not not_4 (not_4_out, b3);
  not not_5 (not_5_out, b2);
  not not_6 (not_6_out, b1);
  not not_7 (not_7_out, b0);
  not not_8 (not_8_out, b0);
  not not_9 (not_9_out, b1);
  not not_10 (not_10_out, b3);
  not not_11 (not_11_out, b0);
  not not_12 (not_12_out, b2);
  not not_13 (not_13_out, b1);
  not not_14 (not_14_out, b2);
  not not_15 (not_15_out, b1);
  not not_16 (not_16_out, b3);
  not not_17 (not_17_out, b1);
  not not_18 (not_18_out, b2);
  not not_19 (not_19_out, b2);
  not not_20 (not_20_out, b3);
  not not_21 (not_21_out, b1);
  not not_22 (not_22_out, b2);
  not not_23 (not_23_out, b0);
  not not_24 (not_24_out, b2);
  not not_25 (not_25_out, b3);
  not not_26 (not_26_out, b1);
  not not_27 (not_27_out, b0);
  not not_28 (not_28_out, b1);
  not not_29 (not_29_out, b2);
  not not_30 (not_30_out, b0);
  not not_31 (not_31_out, b2);
  not not_32 (not_32_out, b0);
  not not_33 (not_33_out, b0);
  not not_34 (not_34_out, b1);
  not not_35 (not_35_out, b2);
  not not_36 (not_36_out, b0);
  not not_37 (not_37_out, b1);
  not not_38 (not_38_out, b3);
  not not_39 (not_39_out, b2);
  not not_40 (not_40_out, b1);
  not not_41 (not_41_out, b3);
  not not_42 (not_42_out, b0);
  not not_43 (not_43_out, b2);
  and and_1 (and_1_out, not_1_out, not_2_out);
  and and_2 (and_2_out, not_3_out, b1);
  and and_3 (and_3_out, not_4_out, b2, b0);
  and and_4 (and_4_out, b2, b1);
  and and_5 (and_5_out, b3, not_5_out, not_6_out);
  and and_6 (and_6_out, b3, not_7_out);
  and and_7 (and_7_out, not_8_out, not_9_out, not_10_out);
  and and_8 (and_8_out, not_11_out, not_12_out);
  and and_9 (and_9_out, not_13_out, not_14_out);
  and and_10 (and_10_out, b0, not_15_out, b3);
  and and_11 (and_11_out, b0, b1, not_16_out);
  and and_12 (and_12_out, not_17_out, not_18_out);
  and and_13 (and_13_out, not_19_out, b3);
  and and_14 (and_14_out, b2, not_20_out);
  and and_15 (and_15_out, b0, not_21_out);
  and and_16 (and_16_out, b0, not_22_out);
  and and_17 (and_17_out, not_23_out, not_24_out, not_25_out);
  and and_18 (and_18_out, not_26_out, b3);
  and and_19 (and_19_out, not_27_out, b1, b2);
  and and_20 (and_20_out, b0, not_28_out, b2);
  and and_21 (and_21_out, b0, b1, not_29_out);
  and and_22 (and_22_out, not_30_out, not_31_out);
  and and_23 (and_23_out, b2, b3);
  and and_24 (and_24_out, not_32_out, b1);
  and and_25 (and_25_out, b1, b3);
  and and_26 (and_26_out, not_33_out, not_34_out);
  and and_27 (and_27_out, not_35_out, b3);
  and and_28 (and_28_out, not_36_out, b2);
  and and_29 (and_29_out, not_37_out, b2, not_38_out);
  and and_30 (and_30_out, b1, b3);
  and and_31 (and_31_out, not_39_out, b3);
  and and_32 (and_32_out, not_40_out, b2, not_41_out);
  and and_33 (and_33_out, not_42_out, b1);
  and and_34 (and_34_out, b1, not_43_out);
  and and_35 (and_35_out, b0, b3);
  or or_1 (a, and_1_out, and_2_out, and_3_out, and_4_out, and_5_out, and_6_out);
  or or_2 (b, and_7_out, and_8_out, and_9_out, and_10_out, and_11_out);
  or or_3 (c, and_12_out, and_13_out, and_14_out, and_15_out, and_16_out);
  or or_4 (d, and_17_out, and_18_out, and_19_out, and_20_out, and_21_out);
  or or_5 (e, and_22_out, and_23_out, and_24_out, and_25_out);
  or or_6 (f, and_26_out, and_27_out, and_28_out, and_29_out, and_30_out);
  or or_7 (g, and_31_out, and_32_out, and_33_out, and_34_out, and_35_out);
endmodule

module counter6 (
  input  B2,
  input  B1,
  input  B0,
  output E2,
  output E1,
  output E0,
  output N
);

  wire and_1_out, and_2_out, and_3_out, and_4_out, and_5_out, and_6_out, not_1_out, not_2_out, not_3_out,
       not_4_out, not_5_out, not_6_out, not_7_out, not_8_out, not_9_out, not_10_out, not_11_out, not_12_out,
       not_13_out, not_14_out;

  not not_1 (not_1_out, B2);
  not not_2 (not_2_out, B1);
  not not_3 (not_3_out, B0);
  not not_4 (not_4_out, B2);
  not not_5 (not_5_out, B1);
  not not_6 (not_6_out, B2);
  not not_7 (not_7_out, B0);
  not not_8 (not_8_out, B2);
  not not_9 (not_9_out, B0);
  not not_10 (not_10_out, B1);
  not not_11 (not_11_out, B0);
  not not_12 (not_12_out, B2);
  not not_13 (not_13_out, B1);
  not not_14 (not_14_out, B0);
  and and_1 (and_1_out, not_1_out, B1, B0);
  and and_2 (and_2_out, B2, not_2_out, not_3_out);
  and and_3 (and_3_out, not_4_out, not_5_out, B0);
  and and_4 (and_4_out, not_6_out, B1, not_7_out);
  and and_5 (and_5_out, not_8_out, not_9_out);
  and and_6 (and_6_out, not_10_out, not_11_out);
  and and_7 (N, not_12_out, not_13_out, not_14_out);
  or or_1 (E2, and_1_out, and_2_out);
  or or_2 (E1, and_3_out, and_4_out);
  or or_3 (E0, and_5_out, and_6_out);
endmodule

module clock24h (
  input  clock_10thsecond,
  input  set_on,
  input  b1_short,
  input  b2_short,
  input  reset,
  output b00,
  output b01,
  output b02,
  output b03,
  output b10,
  output b11,
  output b12,
  output b13,
  output b20,
  output b21,
  output b22,
  output b23,
  output b30,
  output b31,
  output b32,
  output b40,
  output b41,
  output b42,
  output b43,
  output b50,
  output b51,
  output b52,
  output b60,
  output b61,
  output b62,
  output b63,
  output b70,
  output b71
);

  wire counter10_1_b0_out, counter10_1_b1_out, counter10_1_b2_out, counter10_1_b3_out, counter10_1_carry,
       counter10_2_b0_out, counter10_2_b1_out, counter10_2_b2_out, counter10_2_b3_out, counter10_2_carry,
       counter10_3_b0_out, counter10_3_b1_out, counter10_3_b2_out, counter10_3_b3_out, counter10_3_carry,
       counter10_4_b0_out, counter10_4_b1_out, counter10_4_b2_out, counter10_4_b3_out, counter10_4_carry,
       counter24_1_carry, counter24_1_e0, counter24_1_e1, counter24_1_e2, counter24_1_e3, counter24_1_z0,
       counter24_1_z1, demultiplexer_1_out0, demultiplexer_1_out1, demultiplexer_1_out2,
       demultiplexer_1_out3, demultiplexer_1_out4, demultiplexer_1_out5, demultiplexer_1_out6,
       L_6bit_counter_ba3864c1_1_e0, L_6bit_counter_ba3864c1_1_e1, L_6bit_counter_ba3864c1_1_e2,
       L_6bit_counter_ba3864c1_1_n, L_6bit_counter_ba3864c1_2_e0, L_6bit_counter_ba3864c1_2_e1,
       L_6bit_counter_ba3864c1_2_e2, L_6bit_counter_ba3864c1_2_n, multiplexer_1_out, multiplexer_2_out,
       multiplexer_3_out, multiplexer_4_out, multiplexer_5_out, multiplexer_6_out, multiplexer_7_out,
       not_1_out;
  wire [2:0] counter_1_q;

  Counter #(.width(3), .max('h7)) counter_1 (
    .clr(not_1_out), .up(1'b1), .clk(b2_short), .Q(counter_1_q));  // open: load, count, D, carry
  not not_1 (not_1_out, set_on);
  Demultiplexer #(.select(3), .enable("false")) demultiplexer_1 (
    .out0(demultiplexer_1_out0), .out1(demultiplexer_1_out1), .out2(demultiplexer_1_out2),
    .out3(demultiplexer_1_out3), .out4(demultiplexer_1_out4), .out5(demultiplexer_1_out5),
    .out6(demultiplexer_1_out6), .in(b1_short), .sel(counter_1_q));  // open: out7
  Multiplexer #(.enable("false")) multiplexer_1 (
    .in0(clock_10thsecond), .in1(demultiplexer_1_out0), .out(multiplexer_1_out), .sel(set_on));
  counter10 counter10_1 (
    .b3(b03), .b2(b02), .b1(b01), .b0(b00), .b3_out(counter10_1_b3_out), .b2_out(counter10_1_b2_out),
    .b1_out(counter10_1_b1_out), .b0_out(counter10_1_b0_out), .carry(counter10_1_carry));
  Multiplexer #(.enable("false")) multiplexer_2 (
    .in0(counter10_1_carry), .in1(demultiplexer_1_out1), .out(multiplexer_2_out), .sel(set_on));
  D_Flip_Flop d_ff_1 (.D(counter10_1_b3_out), .clk(multiplexer_1_out), .Q(b03), .reset(reset));  // open: Qn, preset
  D_Flip_Flop d_ff_2 (.D(counter10_1_b2_out), .clk(multiplexer_1_out), .Q(b02), .reset(reset));  // open: Qn, preset
  D_Flip_Flop d_ff_3 (.D(counter10_1_b1_out), .clk(multiplexer_1_out), .Q(b01), .reset(reset));  // open: Qn, preset
  D_Flip_Flop d_ff_4 (.D(counter10_1_b0_out), .clk(multiplexer_1_out), .Q(b00), .reset(reset));  // open: Qn, preset
  counter10 counter10_2 (
    .b3(b13), .b2(b12), .b1(b11), .b0(b10), .b3_out(counter10_2_b3_out), .b2_out(counter10_2_b2_out),
    .b1_out(counter10_2_b1_out), .b0_out(counter10_2_b0_out), .carry(counter10_2_carry));
  Multiplexer #(.enable("false")) multiplexer_3 (
    .in0(counter10_2_carry), .in1(demultiplexer_1_out2), .out(multiplexer_3_out), .sel(set_on));
  D_Flip_Flop d_ff_5 (.D(counter10_2_b3_out), .clk(multiplexer_2_out), .Q(b13), .reset(reset));  // open: Qn, preset
  D_Flip_Flop d_ff_6 (.D(counter10_2_b2_out), .clk(multiplexer_2_out), .Q(b12), .reset(reset));  // open: Qn, preset
  D_Flip_Flop d_ff_7 (.D(counter10_2_b1_out), .clk(multiplexer_2_out), .Q(b11), .reset(reset));  // open: Qn, preset
  D_Flip_Flop d_ff_8 (.D(counter10_2_b0_out), .clk(multiplexer_2_out), .Q(b10), .reset(reset));  // open: Qn, preset
  counter10 counter10_3 (
    .b3(b23), .b2(b22), .b1(b21), .b0(b20), .b3_out(counter10_3_b3_out), .b2_out(counter10_3_b2_out),
    .b1_out(counter10_3_b1_out), .b0_out(counter10_3_b0_out), .carry(counter10_3_carry));
  Multiplexer #(.enable("false")) multiplexer_4 (
    .in0(counter10_3_carry), .in1(demultiplexer_1_out3), .out(multiplexer_4_out), .sel(set_on));
  D_Flip_Flop d_ff_9 (.D(counter10_3_b3_out), .clk(multiplexer_3_out), .Q(b23), .reset(reset));  // open: Qn, preset
  D_Flip_Flop d_ff_10 (.D(counter10_3_b2_out), .clk(multiplexer_3_out), .Q(b22), .reset(reset));  // open: Qn, preset
  D_Flip_Flop d_ff_11 (.D(counter10_3_b1_out), .clk(multiplexer_3_out), .Q(b21), .reset(reset));  // open: Qn, preset
  D_Flip_Flop d_ff_12 (.D(counter10_3_b0_out), .clk(multiplexer_3_out), .Q(b20), .reset(reset));  // open: Qn, preset
  counter6 L_6bit_counter_ba3864c1_1 (
    .B2(b32), .B1(b31), .B0(b30), .E2(L_6bit_counter_ba3864c1_1_e2), .E1(L_6bit_counter_ba3864c1_1_e1),
    .E0(L_6bit_counter_ba3864c1_1_e0), .N(L_6bit_counter_ba3864c1_1_n));
  Multiplexer #(.enable("false")) multiplexer_5 (
    .in0(L_6bit_counter_ba3864c1_1_n), .in1(demultiplexer_1_out4), .out(multiplexer_5_out), .sel(set_on));
  D_Flip_Flop d_ff_13 (
    .D(L_6bit_counter_ba3864c1_1_e2), .clk(multiplexer_4_out), .Q(b32), .reset(reset));  // open: Qn, preset
  D_Flip_Flop d_ff_14 (
    .D(L_6bit_counter_ba3864c1_1_e1), .clk(multiplexer_4_out), .Q(b31), .reset(reset));  // open: Qn, preset
  D_Flip_Flop d_ff_15 (
    .D(L_6bit_counter_ba3864c1_1_e0), .clk(multiplexer_4_out), .Q(b30), .reset(reset));  // open: Qn, preset
  counter10 counter10_4 (
    .b3(b43), .b2(b42), .b1(b41), .b0(b40), .b3_out(counter10_4_b3_out), .b2_out(counter10_4_b2_out),
    .b1_out(counter10_4_b1_out), .b0_out(counter10_4_b0_out), .carry(counter10_4_carry));
  Multiplexer #(.enable("false")) multiplexer_6 (
    .in0(counter10_4_carry), .in1(demultiplexer_1_out5), .out(multiplexer_6_out), .sel(set_on));
  D_Flip_Flop d_ff_16 (.D(counter10_4_b3_out), .clk(multiplexer_5_out), .Q(b43), .reset(reset));  // open: Qn, preset
  D_Flip_Flop d_ff_17 (.D(counter10_4_b2_out), .clk(multiplexer_5_out), .Q(b42), .reset(reset));  // open: Qn, preset
  D_Flip_Flop d_ff_18 (.D(counter10_4_b1_out), .clk(multiplexer_5_out), .Q(b41), .reset(reset));  // open: Qn, preset
  D_Flip_Flop d_ff_19 (.D(counter10_4_b0_out), .clk(multiplexer_5_out), .Q(b40), .reset(reset));  // open: Qn, preset
  counter6 L_6bit_counter_ba3864c1_2 (
    .B2(b52), .B1(b51), .B0(b50), .E2(L_6bit_counter_ba3864c1_2_e2), .E1(L_6bit_counter_ba3864c1_2_e1),
    .E0(L_6bit_counter_ba3864c1_2_e0), .N(L_6bit_counter_ba3864c1_2_n));
  Multiplexer #(.enable("false")) multiplexer_7 (
    .in0(L_6bit_counter_ba3864c1_2_n), .in1(demultiplexer_1_out6), .out(multiplexer_7_out), .sel(set_on));
  D_Flip_Flop d_ff_20 (
    .D(L_6bit_counter_ba3864c1_2_e2), .clk(multiplexer_6_out), .Q(b52), .reset(reset));  // open: Qn, preset
  D_Flip_Flop d_ff_21 (
    .D(L_6bit_counter_ba3864c1_2_e1), .clk(multiplexer_6_out), .Q(b51), .reset(reset));  // open: Qn, preset
  D_Flip_Flop d_ff_22 (
    .D(L_6bit_counter_ba3864c1_2_e0), .clk(multiplexer_6_out), .Q(b50), .reset(reset));  // open: Qn, preset
  counter24 counter24_1 (
    .z1_in(b71), .z0_in(b70), .b3(b63), .b2(b62), .b1(b61), .b0(b60), .z1(counter24_1_z1),
    .z0(counter24_1_z0), .e3(counter24_1_e3), .e2(counter24_1_e2), .e1(counter24_1_e1), .e0(counter24_1_e0),
    .carry(counter24_1_carry));
  D_Flip_Flop d_ff_23 (.D(counter24_1_z1), .clk(multiplexer_7_out), .Q(b71), .reset(reset));  // open: Qn, preset
  D_Flip_Flop d_ff_24 (.D(counter24_1_z0), .clk(multiplexer_7_out), .Q(b70), .reset(reset));  // open: Qn, preset
  D_Flip_Flop d_ff_25 (.D(counter24_1_e3), .clk(multiplexer_7_out), .Q(b63), .reset(reset));  // open: Qn, preset
  D_Flip_Flop d_ff_26 (.D(counter24_1_e2), .clk(multiplexer_7_out), .Q(b62), .reset(reset));  // open: Qn, preset
  D_Flip_Flop d_ff_27 (.D(counter24_1_e1), .clk(multiplexer_7_out), .Q(b61), .reset(reset));  // open: Qn, preset
  D_Flip_Flop d_ff_28 (.D(counter24_1_e0), .clk(multiplexer_7_out), .Q(b60), .reset(reset));  // open: Qn, preset
endmodule

module clock24h_display (
  input  clk_10ths,
  input  set_on,
  input  b1_short,
  input  b2_short,
  input  reset,
  output [6:0] x7_0,
  output [6:0] x7_1,
  output [6:0] x7_2,
  output [6:0] x7_3,
  output [6:0] x7_4,
  output [6:0] x7_5,
  output [6:0] x7_6,
  output [6:0] x7_7
);

  wire clock24h_1_b00, clock24h_1_b01, clock24h_1_b02, clock24h_1_b03, clock24h_1_b10, clock24h_1_b11,
       clock24h_1_b12, clock24h_1_b13, clock24h_1_b20, clock24h_1_b21, clock24h_1_b22, clock24h_1_b23,
       clock24h_1_b30, clock24h_1_b31, clock24h_1_b32, clock24h_1_b40, clock24h_1_b41, clock24h_1_b42,
       clock24h_1_b43, clock24h_1_b50, clock24h_1_b51, clock24h_1_b52, clock24h_1_b60, clock24h_1_b61,
       clock24h_1_b62, clock24h_1_b63, clock24h_1_b70, clock24h_1_b71;

  clock24h clock24h_1 (
    .clock_10thsecond(clk_10ths), .set_on(set_on), .b1_short(b1_short), .b2_short(b2_short), .reset(reset),
    .b00(clock24h_1_b00), .b01(clock24h_1_b01), .b02(clock24h_1_b02), .b03(clock24h_1_b03),
    .b10(clock24h_1_b10), .b11(clock24h_1_b11), .b12(clock24h_1_b12), .b13(clock24h_1_b13),
    .b20(clock24h_1_b20), .b21(clock24h_1_b21), .b22(clock24h_1_b22), .b23(clock24h_1_b23),
    .b30(clock24h_1_b30), .b31(clock24h_1_b31), .b32(clock24h_1_b32), .b40(clock24h_1_b40),
    .b41(clock24h_1_b41), .b42(clock24h_1_b42), .b43(clock24h_1_b43), .b50(clock24h_1_b50),
    .b51(clock24h_1_b51), .b52(clock24h_1_b52), .b60(clock24h_1_b60), .b61(clock24h_1_b61),
    .b62(clock24h_1_b62), .b63(clock24h_1_b63), .b70(clock24h_1_b70), .b71(clock24h_1_b71));
  bin2display bin2display_8 (
    .b0(clock24h_1_b70), .b1(clock24h_1_b71), .b2(1'b0), .b3(1'b0), .a(x7_7[0]), .b(x7_7[1]), .c(x7_7[2]),
    .d(x7_7[3]), .e(x7_7[4]), .f(x7_7[5]), .g(x7_7[6]));
  bin2display bin2display_7 (
    .b0(clock24h_1_b60), .b1(clock24h_1_b61), .b2(clock24h_1_b62), .b3(clock24h_1_b63), .a(x7_6[0]),
    .b(x7_6[1]), .c(x7_6[2]), .d(x7_6[3]), .e(x7_6[4]), .f(x7_6[5]), .g(x7_6[6]));
  bin2display bin2display_6 (
    .b0(clock24h_1_b50), .b1(clock24h_1_b51), .b2(clock24h_1_b52), .b3(1'b0), .a(x7_5[0]), .b(x7_5[1]),
    .c(x7_5[2]), .d(x7_5[3]), .e(x7_5[4]), .f(x7_5[5]), .g(x7_5[6]));
  bin2display bin2display_5 (
    .b0(clock24h_1_b40), .b1(clock24h_1_b41), .b2(clock24h_1_b42), .b3(clock24h_1_b43), .a(x7_4[0]),
    .b(x7_4[1]), .c(x7_4[2]), .d(x7_4[3]), .e(x7_4[4]), .f(x7_4[5]), .g(x7_4[6]));
  bin2display bin2display_4 (
    .b0(clock24h_1_b30), .b1(clock24h_1_b31), .b2(clock24h_1_b32), .b3(1'b0), .a(x7_3[0]), .b(x7_3[1]),
    .c(x7_3[2]), .d(x7_3[3]), .e(x7_3[4]), .f(x7_3[5]), .g(x7_3[6]));
  bin2display bin2display_3 (
    .b0(clock24h_1_b20), .b1(clock24h_1_b21), .b2(clock24h_1_b22), .b3(clock24h_1_b23), .a(x7_2[0]),
    .b(x7_2[1]), .c(x7_2[2]), .d(x7_2[3]), .e(x7_2[4]), .f(x7_2[5]), .g(x7_2[6]));
  bin2display bin2display_2 (
    .b0(clock24h_1_b10), .b1(clock24h_1_b11), .b2(clock24h_1_b12), .b3(clock24h_1_b13), .a(x7_1[0]),
    .b(x7_1[1]), .c(x7_1[2]), .d(x7_1[3]), .e(x7_1[4]), .f(x7_1[5]), .g(x7_1[6]));
  bin2display bin2display_1 (
    .b0(clock24h_1_b00), .b1(clock24h_1_b01), .b2(clock24h_1_b02), .b3(clock24h_1_b03), .a(x7_0[0]),
    .b(x7_0[1]), .c(x7_0[2]), .d(x7_0[3]), .e(x7_0[4]), .f(x7_0[5]), .g(x7_0[6]));
endmodule

module counter24 (
  input  z1_in,
  input  z0_in,
  input  b3,
  input  b2,
  input  b1,
  input  b0,
  output z1,
  output z0,
  output e3,
  output e2,
  output e1,
  output e0,
  output carry
);

  wire and_1_out, and_2_out, and_3_out, and_4_out, and_5_out, and_6_out, and_7_out, and_8_out, and_9_out,
       and_10_out, and_11_out, and_12_out, and_13_out, and_14_out, and_15_out, and_16_out, and_17_out,
       and_18_out, not_1_out, not_2_out, not_3_out, not_4_out, not_5_out, not_6_out, not_7_out, not_8_out,
       not_9_out, not_10_out, not_11_out, not_12_out, not_13_out, not_14_out, not_15_out, not_16_out,
       not_17_out, not_18_out, not_19_out, not_20_out, not_21_out, not_22_out, not_23_out, not_24_out,
       not_25_out, not_26_out, not_27_out, not_28_out, not_29_out, not_30_out, not_31_out, not_32_out,
       not_33_out, not_34_out, not_35_out, not_36_out, not_37_out, not_38_out, not_39_out, not_40_out,
       not_41_out, not_42_out, not_43_out, not_44_out, not_45_out, not_46_out, not_47_out, not_48_out,
       not_49_out, not_50_out, not_51_out, not_52_out, not_53_out, not_54_out, not_55_out, not_56_out,
       not_57_out, not_58_out, not_59_out, not_60_out, not_61_out, not_62_out, not_63_out, not_64_out,
       not_65_out, not_66_out, not_67_out;

  not not_1 (not_1_out, z1_in);
  not not_2 (not_2_out, b2);
  not not_3 (not_3_out, b1);
  not not_4 (not_4_out, z0_in);
  not not_5 (not_5_out, b3);
  not not_6 (not_6_out, b2);
  not not_7 (not_7_out, b1);
  not not_8 (not_8_out, z0_in);
  not not_9 (not_9_out, b3);
  not not_10 (not_10_out, b2);
  not not_11 (not_11_out, b0);
  not not_12 (not_12_out, z1_in);
  not not_13 (not_13_out, z0_in);
  not not_14 (not_14_out, b2);
  not not_15 (not_15_out, b1);
  not not_16 (not_16_out, z1_in);
  not not_17 (not_17_out, b3);
  not not_18 (not_18_out, z1_in);
  not not_19 (not_19_out, b2);
  not not_20 (not_20_out, b1);
  not not_21 (not_21_out, b0);
  not not_22 (not_22_out, z1_in);
  not not_23 (not_23_out, b3);
  not not_24 (not_24_out, z1_in);
  not not_25 (not_25_out, b2);
  not not_26 (not_26_out, b1);
  not not_27 (not_27_out, b0);
  not not_28 (not_28_out, z1_in);
  not not_29 (not_29_out, b3);
  not not_30 (not_30_out, b2);
  not not_31 (not_31_out, z1_in);
  not not_32 (not_32_out, b3);
  not not_33 (not_33_out, b1);
  not not_34 (not_34_out, z1_in);
  not not_35 (not_35_out, b3);
  not not_36 (not_36_out, b0);
  not not_37 (not_37_out, z1_in);
  not not_38 (not_38_out, b3);
  not not_39 (not_39_out, b1);
  not not_40 (not_40_out, z0_in);
  not not_41 (not_41_out, b3);
  not not_42 (not_42_out, b2);
  not not_43 (not_43_out, b1);
  not not_44 (not_44_out, z1_in);
  not not_45 (not_45_out, b3);
  not not_46 (not_46_out, b0);
  not not_47 (not_47_out, z0_in);
  not not_48 (not_48_out, b3);
  not not_49 (not_49_out, b2);
  not not_50 (not_50_out, b0);
  not not_51 (not_51_out, z1_in);
  not not_52 (not_52_out, b3);
  not not_53 (not_53_out, b0);
  not not_54 (not_54_out, z1_in);
  not not_55 (not_55_out, b2);
  not not_56 (not_56_out, b1);
  not not_57 (not_57_out, b0);
  not not_58 (not_58_out, z0_in);
  not not_59 (not_59_out, b3);
  not not_60 (not_60_out, b2);
  not not_61 (not_61_out, b0);
  not not_62 (not_62_out, z1_in);
  not not_63 (not_63_out, z0_in);
  not not_64 (not_64_out, b3);
  not not_65 (not_65_out, b2);
  not not_66 (not_66_out, b1);
  not not_67 (not_67_out, b0);
  and and_1 (and_1_out, not_1_out, z0_in, b3, not_2_out, not_3_out, b0);
  and and_2 (and_2_out, z1_in, not_4_out, not_5_out, not_6_out, not_7_out);
  and and_3 (and_3_out, z1_in, not_8_out, not_9_out, not_10_out, not_11_out);
  and and_4 (and_4_out, not_12_out, not_13_out, b3, not_14_out, not_15_out, b0);
  and and_5 (and_5_out, not_16_out, z0_in, not_17_out);
  and and_6 (and_6_out, not_18_out, z0_in, not_19_out, not_20_out, not_21_out);
  and and_7 (and_7_out, not_22_out, not_23_out, b2, b1, b0);
  and and_8 (and_8_out, not_24_out, b3, not_25_out, not_26_out, not_27_out);
  and and_9 (and_9_out, not_28_out, not_29_out, not_30_out, b1, b0);
  and and_10 (and_10_out, not_31_out, not_32_out, b2, not_33_out);
  and and_11 (and_11_out, not_34_out, not_35_out, b2, not_36_out);
  and and_12 (and_12_out, not_37_out, not_38_out, not_39_out, b0);
  and and_13 (and_13_out, not_40_out, not_41_out, not_42_out, not_43_out, b0);
  and and_14 (and_14_out, not_44_out, not_45_out, b1, not_46_out);
  and and_15 (and_15_out, not_47_out, not_48_out, not_49_out, b1, not_50_out);
  and and_16 (and_16_out, not_51_out, not_52_out, not_53_out);
  and and_17 (and_17_out, not_54_out, not_55_out, not_56_out, not_57_out);
  and and_18 (and_18_out, not_58_out, not_59_out, not_60_out, not_61_out);
  and and_19 (carry, not_62_out, not_63_out, not_64_out, not_65_out, not_66_out, not_67_out);
  or or_1 (z1, and_1_out, and_2_out, and_3_out);
  or or_2 (z0, and_4_out, and_5_out, and_6_out);
  or or_3 (e3, and_7_out, and_8_out);
  or or_4 (e2, and_9_out, and_10_out, and_11_out);
  or or_5 (e1, and_12_out, and_13_out, and_14_out, and_15_out);
  or or_6 (e0, and_16_out, and_17_out, and_18_out);
endmodule

module input_ctrl (
  input  button,
  input  clk,
  output short,
  output long
);

  wire and_1_out, d_ff_1_q, d_ff_2_q, d_ff_3_q, not_1_out, not_2_out, not_3_out, or_1_out;
  wire [7:0] counter_1_q;

  not not_1 (not_1_out, button);
  D_Flip_Flop d_ff_1 (.D(button), .clk(clk), .Q(d_ff_1_q));  // open: Qn, preset, reset
  Counter counter_1 (
    .clr(not_1_out), .load(counter_1_q[6]), .up(1'b1), .clk(clk), .D(counter_1_q), .Q(counter_1_q));  // open: count, carry
  D_Flip_Flop #(.trigger("falling")) d_ff_2 (
    .D(d_ff_1_q), .clk(button), .Q(d_ff_2_q), .reset(or_1_out));  // open: Qn, preset
  or or_1 (or_1_out, long, and_1_out);
  D_Flip_Flop d_ff_3 (.D(d_ff_2_q), .clk(clk), .Q(d_ff_3_q), .reset(long));  // open: Qn, preset
  and and_1 (and_1_out, d_ff_3_q, not_2_out);
  not not_2 (not_2_out, long);
  not not_3 (not_3_out, counter_1_q[6]);
  D_Flip_Flop d_ff_4 (.D(counter_1_q[6]), .clk(clk), .Q(long));  // open: Qn, preset, reset
  and and_2 (short, d_ff_3_q, not_3_out);

  // Notes on the sheet:
  //   Signal at the end when the button is released
  //   Connect to a pin to choose the duration of "long"
endmodule

module main_statemachine_logic (
  input  state_bit2,
  input  state_bit1,
  input  state_bit0,
  input  button1_short,
  input  button2_short,
  input  Dipswitch1,
  output nextstate_bit2,
  output nextstate_bit1,
  output nextstate_bit0
);

  wire and_1_out, and_2_out, and_3_out, and_4_out, and_5_out, and_6_out, and_7_out, and_8_out, and_9_out,
       and_10_out, and_11_out, and_12_out, and_13_out, and_14_out, and_15_out, and_16_out, and_17_out,
       and_18_out, and_19_out, and_20_out, not_1_out, not_2_out, not_3_out, not_4_out, not_5_out, not_6_out,
       not_7_out, not_8_out, not_9_out, not_10_out, not_11_out, not_12_out, not_13_out, not_14_out,
       not_15_out, not_16_out, not_17_out, not_18_out, not_19_out, not_20_out, not_21_out, not_22_out,
       not_23_out, not_24_out, not_25_out, not_26_out, not_27_out, not_28_out, not_29_out, not_30_out,
       not_31_out, not_32_out, not_33_out;

  not not_1 (not_1_out, state_bit2);
  not not_2 (not_2_out, state_bit1);
  not not_3 (not_3_out, state_bit0);
  not not_4 (not_4_out, button2_short);
  not not_5 (not_5_out, button1_short);
  not not_6 (not_6_out, state_bit1);
  not not_7 (not_7_out, button1_short);
  not not_8 (not_8_out, Dipswitch1);
  not not_9 (not_9_out, state_bit1);
  not not_10 (not_10_out, button2_short);
  not not_11 (not_11_out, state_bit1);
  not not_12 (not_12_out, state_bit0);
  not not_13 (not_13_out, button2_short);
  not not_14 (not_14_out, state_bit1);
  not not_15 (not_15_out, button1_short);
  not not_16 (not_16_out, button1_short);
  not not_17 (not_17_out, button2_short);
  not not_18 (not_18_out, Dipswitch1);
  not not_19 (not_19_out, state_bit2);
  not not_20 (not_20_out, state_bit0);
  not not_21 (not_21_out, state_bit2);
  not not_22 (not_22_out, state_bit0);
  not not_23 (not_23_out, button1_short);
  not not_24 (not_24_out, state_bit1);
  not not_25 (not_25_out, state_bit0);
  not not_26 (not_26_out, button1_short);
  not not_27 (not_27_out, button1_short);
  not not_28 (not_28_out, button2_short);
  not not_29 (not_29_out, Dipswitch1);
  not not_30 (not_30_out, state_bit0);
  not not_31 (not_31_out, button2_short);
  not not_32 (not_32_out, state_bit0);
  not not_33 (not_33_out, button2_short);
  and and_1 (and_1_out, not_1_out, not_2_out, not_3_out, button1_short, not_4_out, Dipswitch1);
  and and_2 (and_2_out, state_bit1, state_bit0, not_5_out, button2_short, Dipswitch1);
  and and_3 (and_3_out, state_bit2, not_6_out, not_7_out);
  and and_4 (and_4_out, state_bit2, not_8_out);
  and and_5 (and_5_out, state_bit2, not_9_out, button2_short);
  and and_6 (and_6_out, state_bit2, state_bit0);
  and and_7 (and_7_out, state_bit2, state_bit1, not_10_out);
  and and_8 (and_8_out, not_11_out, not_12_out, button1_short, not_13_out, Dipswitch1);
  and and_9 (and_9_out, not_14_out, state_bit0, not_15_out, button2_short, Dipswitch1);
  and and_10 (and_10_out, state_bit1, not_16_out, not_17_out);
  and and_11 (and_11_out, state_bit1, not_18_out);
  and and_12 (and_12_out, not_19_out, state_bit1, not_20_out, button2_short);
  and and_13 (and_13_out, state_bit1, state_bit0, button1_short);
  and and_14 (and_14_out, not_21_out, not_22_out, not_23_out, button2_short, Dipswitch1);
  and and_15 (and_15_out, not_24_out, not_25_out, not_26_out, button2_short, Dipswitch1);
  and and_16 (and_16_out, state_bit0, not_27_out, not_28_out);
  and and_17 (and_17_out, state_bit0, not_29_out);
  and and_18 (and_18_out, state_bit0, button1_short, button2_short);
  and and_19 (and_19_out, state_bit1, not_30_out, button1_short, not_31_out, Dipswitch1);
  and and_20 (and_20_out, state_bit2, not_32_out, button1_short, not_33_out, Dipswitch1);
  or or_1 (nextstate_bit2, and_1_out, and_2_out, and_3_out, and_4_out, and_5_out, and_6_out, and_7_out);
  or or_2 (nextstate_bit1, and_8_out, and_9_out, and_10_out, and_11_out, and_12_out, and_13_out);
  or or_3 (nextstate_bit0, and_14_out, and_15_out, and_16_out, and_17_out, and_18_out, and_19_out, and_20_out);
endmodule

module main_statemachine (
  input  button1_short,
  input  button2_short,
  input  dippswitch1,
  input  clk,
  output [2:0] state_binary
);

  wire main_statemachine_logic_1_nextstate_bit0, main_statemachine_logic_1_nextstate_bit1,
       main_statemachine_logic_1_nextstate_bit2;

  main_statemachine_logic main_statemachine_logic_1 (
    .state_bit2(state_binary[2]), .state_bit1(state_binary[1]), .state_bit0(state_binary[0]),
    .button1_short(button1_short), .button2_short(button2_short), .Dipswitch1(dippswitch1),
    .nextstate_bit2(main_statemachine_logic_1_nextstate_bit2),
    .nextstate_bit1(main_statemachine_logic_1_nextstate_bit1),
    .nextstate_bit0(main_statemachine_logic_1_nextstate_bit0));
  D_Flip_Flop d_ff_1 (
    .D(main_statemachine_logic_1_nextstate_bit2), .clk(clk), .Q(state_binary[2]));  // open: Qn, preset, reset
  D_Flip_Flop d_ff_2 (
    .D(main_statemachine_logic_1_nextstate_bit1), .clk(clk), .Q(state_binary[1]));  // open: Qn, preset, reset
  D_Flip_Flop d_ff_3 (
    .D(main_statemachine_logic_1_nextstate_bit0), .clk(clk), .Q(state_binary[0]));  // open: Qn, preset, reset
endmodule

module L_3bit_to_state_47837c81 (
  input  bit2,
  input  bit1,
  input  bit0,
  output state_0,
  output state_1,
  output state_2,
  output state_3,
  output state_4,
  output state_5,
  output state_6
);

  wire not_1_out, not_2_out, not_3_out, not_4_out, not_5_out, not_6_out, not_7_out, not_8_out, not_9_out,
       not_10_out, not_11_out, not_12_out;

  not not_1 (not_1_out, bit2);
  not not_2 (not_2_out, bit1);
  not not_3 (not_3_out, bit0);
  not not_4 (not_4_out, bit2);
  not not_5 (not_5_out, bit1);
  not not_6 (not_6_out, bit2);
  not not_7 (not_7_out, bit0);
  not not_8 (not_8_out, bit2);
  not not_9 (not_9_out, bit1);
  not not_10 (not_10_out, bit0);
  not not_11 (not_11_out, bit1);
  not not_12 (not_12_out, bit0);
  and and_1 (state_0, not_1_out, not_2_out, not_3_out);
  and and_2 (state_1, not_4_out, not_5_out, bit0);
  and and_3 (state_2, not_6_out, bit1, not_7_out);
  and and_4 (state_3, not_8_out, bit1, bit0);
  and and_5 (state_4, bit2, not_9_out, not_10_out);
  and and_6 (state_5, bit2, not_11_out, bit0);
  and and_7 (state_6, bit2, bit1, not_12_out);
endmodule

module state0 (
  input  state_on,
  input  [3:0] buttons,
  output out_3
);

  not not_1 (out_3, state_on);
  clock24h_display clock24h_display_1 ();  // open: clk_10ths, set_on, b1_short, b2_short, reset, x7_0, x7_1, x7_2, x7_3, x7_4, x7_5, x7_6, x7_7
endmodule
